// Logisim project sqrt2.circ as structural Verilog: 12 circuits, main circuit main
module main (
  input  ENABLE,
  input  [15:0] IO_DATA_IN,
  output NAN,
  output PINF,
  output NINF,
  output RESULT,
  output [15:0] IO_DATA_OUT
);

  wire CLK_out;

  Clock CLK (.out(CLK_out));
  sqrt sqrt_1 (
    .CLK(CLK_out), .ENABLE(ENABLE), .IO_DATA_IN(IO_DATA_IN), .IS_NAN(NAN), .IS_PINF(PINF), .IS_NINF(NINF),
    .RESULT(RESULT), .IO_DATA_OUT(IO_DATA_OUT));
endmodule

module sqrt (
  input  CLK,
  input  ENABLE,
  input  [15:0] IO_DATA_IN,
  output IS_NAN,
  output IS_PINF,
  output IS_NINF,
  output RESULT,
  output [15:0] IO_DATA_OUT
);


  assign IO_DATA_OUT = IO_DATA_IN;
endmodule

module shift_left (
  input  [15:0] IO_IN,
  output [15:0] IO_OUT
);


  assign IO_OUT = {IO_IN[14:0], 1'b0};
endmodule

module substructor (
  input  borrow_in,
  input  minuend,
  input  subtrahend,
  output difference,
  output borrow_out
);

  wire and_1_out, and_2_out, not_1_out, not_2_out, xor_1_out;

  not not_1 (not_1_out, minuend);
  xor xor_1 (xor_1_out, minuend, subtrahend);
  and and_1 (and_1_out, subtrahend, not_1_out);
  not not_2 (not_2_out, xor_1_out);
  and and_2 (and_2_out, not_2_out, borrow_in);
  xor xor_2 (difference, borrow_in, xor_1_out);
  or or_1 (borrow_out, and_2_out, and_1_out);
endmodule

module substructor_16bit (
  input  [15:0] subtrahend,
  input  [15:0] minuend,
  output [15:0] difference
);

  wire substructor_1_borrow_out, substructor_2_borrow_out, substructor_3_borrow_out,
       substructor_4_borrow_out, substructor_5_borrow_out, substructor_6_borrow_out,
       substructor_7_borrow_out, substructor_8_borrow_out, substructor_9_borrow_out,
       substructor_10_borrow_out, substructor_11_borrow_out, substructor_12_borrow_out,
       substructor_13_borrow_out, substructor_14_borrow_out, substructor_15_borrow_out,
       substructor_16_borrow_out;

  substructor substructor_1 (
    .borrow_in(1'b0), .minuend(minuend[0]), .subtrahend(subtrahend[0]), .difference(difference[0]),
    .borrow_out(substructor_1_borrow_out));
  substructor substructor_2 (
    .borrow_in(substructor_1_borrow_out), .minuend(minuend[1]), .subtrahend(subtrahend[1]),
    .difference(difference[1]), .borrow_out(substructor_2_borrow_out));
  substructor substructor_3 (
    .borrow_in(substructor_2_borrow_out), .minuend(minuend[2]), .subtrahend(subtrahend[2]),
    .difference(difference[2]), .borrow_out(substructor_3_borrow_out));
  substructor substructor_4 (
    .borrow_in(substructor_3_borrow_out), .minuend(minuend[3]), .subtrahend(subtrahend[3]),
    .difference(difference[3]), .borrow_out(substructor_4_borrow_out));
  substructor substructor_5 (
    .borrow_in(substructor_4_borrow_out), .minuend(minuend[4]), .subtrahend(subtrahend[4]),
    .difference(difference[4]), .borrow_out(substructor_5_borrow_out));
  substructor substructor_6 (
    .borrow_in(substructor_5_borrow_out), .minuend(minuend[5]), .subtrahend(subtrahend[5]),
    .difference(difference[5]), .borrow_out(substructor_6_borrow_out));
  substructor substructor_7 (
    .borrow_in(substructor_6_borrow_out), .minuend(minuend[6]), .subtrahend(subtrahend[6]),
    .difference(difference[6]), .borrow_out(substructor_7_borrow_out));
  substructor substructor_8 (
    .borrow_in(substructor_7_borrow_out), .minuend(minuend[7]), .subtrahend(subtrahend[7]),
    .difference(difference[7]), .borrow_out(substructor_8_borrow_out));
  substructor substructor_9 (
    .borrow_in(substructor_8_borrow_out), .minuend(minuend[8]), .subtrahend(subtrahend[8]),
    .difference(difference[8]), .borrow_out(substructor_9_borrow_out));
  substructor substructor_10 (
    .borrow_in(substructor_9_borrow_out), .minuend(minuend[9]), .subtrahend(subtrahend[9]),
    .difference(difference[9]), .borrow_out(substructor_10_borrow_out));
  substructor substructor_11 (
    .borrow_in(substructor_10_borrow_out), .minuend(minuend[10]), .subtrahend(subtrahend[10]),
    .difference(difference[10]), .borrow_out(substructor_11_borrow_out));
  substructor substructor_12 (
    .borrow_in(substructor_11_borrow_out), .minuend(minuend[11]), .subtrahend(subtrahend[11]),
    .difference(difference[11]), .borrow_out(substructor_12_borrow_out));
  substructor substructor_13 (
    .borrow_in(substructor_12_borrow_out), .minuend(minuend[12]), .subtrahend(subtrahend[12]),
    .difference(difference[12]), .borrow_out(substructor_13_borrow_out));
  substructor substructor_14 (
    .borrow_in(substructor_13_borrow_out), .minuend(minuend[13]), .subtrahend(subtrahend[13]),
    .difference(difference[13]), .borrow_out(substructor_14_borrow_out));
  substructor substructor_15 (
    .borrow_in(substructor_14_borrow_out), .minuend(minuend[14]), .subtrahend(subtrahend[14]),
    .difference(difference[14]), .borrow_out(substructor_15_borrow_out));
  substructor substructor_16 (
    .borrow_in(substructor_15_borrow_out), .minuend(minuend[15]), .subtrahend(subtrahend[15]),
    .difference(difference[15]), .borrow_out(substructor_16_borrow_out));
endmodule

module comparator_1bit (
  input  A,
  input  B,
  input  oldA_smaller_oldB,
  input  oldA_equal_oldB,
  input  oldA_bigger_oldB,
  output A_smaller_B,
  output A_equal_B,
  output A_bigger_B
);

  wire and_1_out, and_2_out, and_3_out, and_5_out, not_1_out, xor_1_out;

  and and_1 (and_1_out, ~A, B);  // AND_Gate
  xor xor_1 (xor_1_out, A, B);
  and and_2 (and_2_out, A, ~B);  // AND_Gate
  not not_1 (not_1_out, xor_1_out);
  and and_3 (and_3_out, oldA_smaller_oldB, not_1_out);
  and and_4 (A_equal_B, not_1_out, oldA_equal_oldB);
  and and_5 (and_5_out, oldA_bigger_oldB, not_1_out);
  or or_1 (A_smaller_B, and_1_out, and_3_out);
  or or_2 (A_bigger_B, and_5_out, and_2_out);
endmodule

module comparator_16bit (
  input  [15:0] B,
  input  [15:0] A,
  output A_smaller_B,
  output A_equal_B,
  output A_bigger_B
);

  wire comparator_1bit_2_a_bigger_b, comparator_1bit_2_a_equal_b, comparator_1bit_2_a_smaller_b,
       comparator_1bit_3_a_bigger_b, comparator_1bit_3_a_equal_b, comparator_1bit_3_a_smaller_b,
       comparator_1bit_4_a_bigger_b, comparator_1bit_4_a_equal_b, comparator_1bit_4_a_smaller_b,
       comparator_1bit_5_a_bigger_b, comparator_1bit_5_a_equal_b, comparator_1bit_5_a_smaller_b,
       comparator_1bit_6_a_bigger_b, comparator_1bit_6_a_equal_b, comparator_1bit_6_a_smaller_b,
       comparator_1bit_7_a_bigger_b, comparator_1bit_7_a_equal_b, comparator_1bit_7_a_smaller_b,
       comparator_1bit_8_a_bigger_b, comparator_1bit_8_a_equal_b, comparator_1bit_8_a_smaller_b,
       comparator_1bit_9_a_bigger_b, comparator_1bit_9_a_equal_b, comparator_1bit_9_a_smaller_b,
       comparator_1bit_10_a_bigger_b, comparator_1bit_10_a_equal_b, comparator_1bit_10_a_smaller_b,
       comparator_1bit_11_a_bigger_b, comparator_1bit_11_a_equal_b, comparator_1bit_11_a_smaller_b,
       comparator_1bit_12_a_bigger_b, comparator_1bit_12_a_equal_b, comparator_1bit_12_a_smaller_b,
       comparator_1bit_13_a_bigger_b, comparator_1bit_13_a_equal_b, comparator_1bit_13_a_smaller_b,
       comparator_1bit_14_a_bigger_b, comparator_1bit_14_a_equal_b, comparator_1bit_14_a_smaller_b,
       comparator_1bit_15_a_bigger_b, comparator_1bit_15_a_equal_b, comparator_1bit_15_a_smaller_b,
       comparator_1bit_16_a_bigger_b, comparator_1bit_16_a_equal_b, comparator_1bit_16_a_smaller_b;

  comparator_1bit comparator_1bit_1 (
    .A(A[15]), .B(B[15]), .oldA_smaller_oldB(comparator_1bit_2_a_smaller_b),
    .oldA_equal_oldB(comparator_1bit_2_a_equal_b), .oldA_bigger_oldB(comparator_1bit_2_a_bigger_b),
    .A_smaller_B(A_smaller_B), .A_equal_B(A_equal_B), .A_bigger_B(A_bigger_B));
  comparator_1bit comparator_1bit_2 (
    .A(A[14]), .B(B[14]), .oldA_smaller_oldB(comparator_1bit_3_a_smaller_b),
    .oldA_equal_oldB(comparator_1bit_3_a_equal_b), .oldA_bigger_oldB(comparator_1bit_3_a_bigger_b),
    .A_smaller_B(comparator_1bit_2_a_smaller_b), .A_equal_B(comparator_1bit_2_a_equal_b),
    .A_bigger_B(comparator_1bit_2_a_bigger_b));
  comparator_1bit comparator_1bit_3 (
    .A(A[13]), .B(B[13]), .oldA_smaller_oldB(comparator_1bit_4_a_smaller_b),
    .oldA_equal_oldB(comparator_1bit_4_a_equal_b), .oldA_bigger_oldB(comparator_1bit_4_a_bigger_b),
    .A_smaller_B(comparator_1bit_3_a_smaller_b), .A_equal_B(comparator_1bit_3_a_equal_b),
    .A_bigger_B(comparator_1bit_3_a_bigger_b));
  comparator_1bit comparator_1bit_4 (
    .A(A[12]), .B(B[12]), .oldA_smaller_oldB(comparator_1bit_5_a_smaller_b),
    .oldA_equal_oldB(comparator_1bit_5_a_equal_b), .oldA_bigger_oldB(comparator_1bit_5_a_bigger_b),
    .A_smaller_B(comparator_1bit_4_a_smaller_b), .A_equal_B(comparator_1bit_4_a_equal_b),
    .A_bigger_B(comparator_1bit_4_a_bigger_b));
  comparator_1bit comparator_1bit_5 (
    .A(A[11]), .B(B[11]), .oldA_smaller_oldB(comparator_1bit_6_a_smaller_b),
    .oldA_equal_oldB(comparator_1bit_6_a_equal_b), .oldA_bigger_oldB(comparator_1bit_6_a_bigger_b),
    .A_smaller_B(comparator_1bit_5_a_smaller_b), .A_equal_B(comparator_1bit_5_a_equal_b),
    .A_bigger_B(comparator_1bit_5_a_bigger_b));
  comparator_1bit comparator_1bit_6 (
    .A(A[10]), .B(B[10]), .oldA_smaller_oldB(comparator_1bit_7_a_smaller_b),
    .oldA_equal_oldB(comparator_1bit_7_a_equal_b), .oldA_bigger_oldB(comparator_1bit_7_a_bigger_b),
    .A_smaller_B(comparator_1bit_6_a_smaller_b), .A_equal_B(comparator_1bit_6_a_equal_b),
    .A_bigger_B(comparator_1bit_6_a_bigger_b));
  comparator_1bit comparator_1bit_7 (
    .A(A[9]), .B(B[9]), .oldA_smaller_oldB(comparator_1bit_8_a_smaller_b),
    .oldA_equal_oldB(comparator_1bit_8_a_equal_b), .oldA_bigger_oldB(comparator_1bit_8_a_bigger_b),
    .A_smaller_B(comparator_1bit_7_a_smaller_b), .A_equal_B(comparator_1bit_7_a_equal_b),
    .A_bigger_B(comparator_1bit_7_a_bigger_b));
  comparator_1bit comparator_1bit_8 (
    .A(A[8]), .B(B[8]), .oldA_smaller_oldB(comparator_1bit_9_a_smaller_b),
    .oldA_equal_oldB(comparator_1bit_9_a_equal_b), .oldA_bigger_oldB(comparator_1bit_9_a_bigger_b),
    .A_smaller_B(comparator_1bit_8_a_smaller_b), .A_equal_B(comparator_1bit_8_a_equal_b),
    .A_bigger_B(comparator_1bit_8_a_bigger_b));
  comparator_1bit comparator_1bit_9 (
    .A(A[7]), .B(B[7]), .oldA_smaller_oldB(comparator_1bit_10_a_smaller_b),
    .oldA_equal_oldB(comparator_1bit_10_a_equal_b), .oldA_bigger_oldB(comparator_1bit_10_a_bigger_b),
    .A_smaller_B(comparator_1bit_9_a_smaller_b), .A_equal_B(comparator_1bit_9_a_equal_b),
    .A_bigger_B(comparator_1bit_9_a_bigger_b));
  comparator_1bit comparator_1bit_10 (
    .A(A[6]), .B(B[6]), .oldA_smaller_oldB(comparator_1bit_11_a_smaller_b),
    .oldA_equal_oldB(comparator_1bit_11_a_equal_b), .oldA_bigger_oldB(comparator_1bit_11_a_bigger_b),
    .A_smaller_B(comparator_1bit_10_a_smaller_b), .A_equal_B(comparator_1bit_10_a_equal_b),
    .A_bigger_B(comparator_1bit_10_a_bigger_b));
  comparator_1bit comparator_1bit_11 (
    .A(A[5]), .B(B[5]), .oldA_smaller_oldB(comparator_1bit_12_a_smaller_b),
    .oldA_equal_oldB(comparator_1bit_12_a_equal_b), .oldA_bigger_oldB(comparator_1bit_12_a_bigger_b),
    .A_smaller_B(comparator_1bit_11_a_smaller_b), .A_equal_B(comparator_1bit_11_a_equal_b),
    .A_bigger_B(comparator_1bit_11_a_bigger_b));
  comparator_1bit comparator_1bit_12 (
    .A(A[4]), .B(B[4]), .oldA_smaller_oldB(comparator_1bit_13_a_smaller_b),
    .oldA_equal_oldB(comparator_1bit_13_a_equal_b), .oldA_bigger_oldB(comparator_1bit_13_a_bigger_b),
    .A_smaller_B(comparator_1bit_12_a_smaller_b), .A_equal_B(comparator_1bit_12_a_equal_b),
    .A_bigger_B(comparator_1bit_12_a_bigger_b));
  comparator_1bit comparator_1bit_13 (
    .A(A[3]), .B(B[3]), .oldA_smaller_oldB(comparator_1bit_14_a_smaller_b),
    .oldA_equal_oldB(comparator_1bit_14_a_equal_b), .oldA_bigger_oldB(comparator_1bit_14_a_bigger_b),
    .A_smaller_B(comparator_1bit_13_a_smaller_b), .A_equal_B(comparator_1bit_13_a_equal_b),
    .A_bigger_B(comparator_1bit_13_a_bigger_b));
  comparator_1bit comparator_1bit_14 (
    .A(A[2]), .B(B[2]), .oldA_smaller_oldB(comparator_1bit_15_a_smaller_b),
    .oldA_equal_oldB(comparator_1bit_15_a_equal_b), .oldA_bigger_oldB(comparator_1bit_15_a_bigger_b),
    .A_smaller_B(comparator_1bit_14_a_smaller_b), .A_equal_B(comparator_1bit_14_a_equal_b),
    .A_bigger_B(comparator_1bit_14_a_bigger_b));
  comparator_1bit comparator_1bit_15 (
    .A(A[1]), .B(B[1]), .oldA_smaller_oldB(comparator_1bit_16_a_smaller_b),
    .oldA_equal_oldB(comparator_1bit_16_a_equal_b), .oldA_bigger_oldB(comparator_1bit_16_a_bigger_b),
    .A_smaller_B(comparator_1bit_15_a_smaller_b), .A_equal_B(comparator_1bit_15_a_equal_b),
    .A_bigger_B(comparator_1bit_15_a_bigger_b));
  comparator_1bit comparator_1bit_16 (
    .A(A[0]), .B(B[0]), .oldA_smaller_oldB(1'b0), .oldA_equal_oldB(1'b1), .oldA_bigger_oldB(1'b0),
    .A_smaller_B(comparator_1bit_16_a_smaller_b), .A_equal_B(comparator_1bit_16_a_equal_b),
    .A_bigger_B(comparator_1bit_16_a_bigger_b));
endmodule

module summator_1bit (
  input  A,
  input  B,
  input  borrow_in,
  output Sum,
  output Borrow_out
);

  wire and_1_out, and_2_out, xor_1_out;

  and and_1 (and_1_out, A, B);
  xor xor_1 (xor_1_out, A, B);
  xor xor_2 (Sum, xor_1_out, borrow_in);
  and and_2 (and_2_out, xor_1_out, borrow_in);
  or or_1 (Borrow_out, and_2_out, and_1_out);
endmodule

module summator_4bit (
  input  [3:0] A,
  input  [3:0] B,
  output [3:0] IO_OUT
);

  wire summator_1bit_1_borrow_out, summator_1bit_2_borrow_out, summator_1bit_3_borrow_out;

  summator_1bit summator_1bit_1 (
    .A(A[0]), .B(B[0]), .borrow_in(1'b0), .Sum(IO_OUT[0]), .Borrow_out(summator_1bit_1_borrow_out));
  summator_1bit summator_1bit_2 (
    .A(A[1]), .B(B[1]), .borrow_in(summator_1bit_1_borrow_out), .Sum(IO_OUT[1]),
    .Borrow_out(summator_1bit_2_borrow_out));
  summator_1bit summator_1bit_3 (
    .A(A[2]), .B(B[2]), .borrow_in(summator_1bit_2_borrow_out), .Sum(IO_OUT[2]),
    .Borrow_out(summator_1bit_3_borrow_out));
  summator_1bit summator_1bit_4 (
    .A(A[3]), .B(B[3]), .borrow_in(summator_1bit_3_borrow_out), .Sum(IO_OUT[3]));  // open: Borrow_out
endmodule

module synch_rs_trigger (
  input  A,
  input  C,
  input  B,
  input  ENABLE,
  output Q,
  output NQ
);

  wire and_1_out, and_2_out, nor_2_out, or_1_out, por_1_out;

  POR por_1 (.out(por_1_out));
  and and_1 (and_1_out, A, C);
  and and_2 (and_2_out, C, B);
  or or_1 (or_1_out, ENABLE, por_1_out);
  nor nor_1 (Q, and_1_out, NQ);
  nor nor_2 (nor_2_out, Q, and_2_out);
  or or_2 (NQ, nor_2_out, or_1_out);
endmodule

module d_trigger (
  input  C,
  input  D,
  input  ENABLE,
  output Q,
  output NQ
);

  wire not_1_out;

  not not_1 (not_1_out, D);
  synch_rs_trigger synch_rs_trigger_1 (.A(not_1_out), .C(C), .B(D), .ENABLE(ENABLE), .Q(Q), .NQ(NQ));
endmodule

module memory_cell_16bit (
  input  [15:0] IO_DATA_IN,
  input  R_or_W,
  input  C,
  input  ENABLE,
  output [15:0] out_5
);

  wire and_1_out;

  and and_1 (and_1_out, R_or_W, C);
  d_trigger d_trigger_1 (.C(and_1_out), .D(IO_DATA_IN[0]), .ENABLE(ENABLE), .Q(out_5[0]));  // open: NQ
  d_trigger d_trigger_2 (.C(and_1_out), .D(IO_DATA_IN[1]), .ENABLE(ENABLE), .Q(out_5[1]));  // open: NQ
  d_trigger d_trigger_3 (.C(and_1_out), .D(IO_DATA_IN[2]), .ENABLE(ENABLE), .Q(out_5[2]));  // open: NQ
  d_trigger d_trigger_4 (.C(and_1_out), .D(IO_DATA_IN[3]), .ENABLE(ENABLE), .Q(out_5[3]));  // open: NQ
  d_trigger d_trigger_5 (.C(and_1_out), .D(IO_DATA_IN[4]), .ENABLE(ENABLE), .Q(out_5[4]));  // open: NQ
  d_trigger d_trigger_6 (.C(and_1_out), .D(IO_DATA_IN[5]), .ENABLE(ENABLE), .Q(out_5[5]));  // open: NQ
  d_trigger d_trigger_7 (.C(and_1_out), .D(IO_DATA_IN[6]), .ENABLE(ENABLE), .Q(out_5[6]));  // open: NQ
  d_trigger d_trigger_8 (.C(and_1_out), .D(IO_DATA_IN[7]), .ENABLE(ENABLE), .Q(out_5[7]));  // open: NQ
  d_trigger d_trigger_9 (.C(and_1_out), .D(IO_DATA_IN[8]), .ENABLE(ENABLE), .Q(out_5[8]));  // open: NQ
  d_trigger d_trigger_10 (.C(and_1_out), .D(IO_DATA_IN[9]), .ENABLE(ENABLE), .Q(out_5[9]));  // open: NQ
  d_trigger d_trigger_11 (.C(and_1_out), .D(IO_DATA_IN[10]), .ENABLE(ENABLE), .Q(out_5[10]));  // open: NQ
  d_trigger d_trigger_12 (.C(and_1_out), .D(IO_DATA_IN[11]), .ENABLE(ENABLE), .Q(out_5[11]));  // open: NQ
  d_trigger d_trigger_13 (.C(and_1_out), .D(IO_DATA_IN[12]), .ENABLE(ENABLE), .Q(out_5[12]));  // open: NQ
  d_trigger d_trigger_14 (.C(and_1_out), .D(IO_DATA_IN[13]), .ENABLE(ENABLE), .Q(out_5[13]));  // open: NQ
  d_trigger d_trigger_15 (.C(and_1_out), .D(IO_DATA_IN[14]), .ENABLE(ENABLE), .Q(out_5[14]));  // open: NQ
  d_trigger d_trigger_16 (.C(and_1_out), .D(IO_DATA_IN[15]), .ENABLE(ENABLE), .Q(out_5[15]));  // open: NQ
endmodule
